# Fritzing sketch Diagrama Electrico (saved by Fritzing 0.9.3b)
breadboards: 1

parts:
  Componente1 = Arduino Mega ADK (Rev3)
  Resistencia_Pull_Down = Resistor [tolerance=±5% resistance=220 part_number="Recistencia Pul Low" package=THT]
  S1 = Pushbutton [package=THT]

nets:
  N1: Componente1.D21/SCL, Resistencia_Pull_Down.Pin_0, S1.leg0
  N2: Componente1.5V, S1.leg1
  N3: Componente1.GND, Resistencia_Pull_Down.Pin_1
